# Fritzing sketch daikin-zigbee-bridge (saved by Fritzing 0.9.3b)
breadboards: 1

parts:
  Zigbee_Thermostat_Bridge = ESP32-C6-DevKitC-1
  Daikin_Controller = ESP32-C6-DevKitC-1

nets:
  N1: Zigbee_Thermostat_Bridge.Pin_14, Daikin_Controller.Pin_14
  N2: Zigbee_Thermostat_Bridge.Pin_15, Zigbee_Thermostat_Bridge.Pin_18, Zigbee_Thermostat_Bridge.Pin_32, Daikin_Controller.Pin_15, Daikin_Controller.Pin_18, Daikin_Controller.Pin_32
  N3: Zigbee_Thermostat_Bridge.Pin_22, Daikin_Controller.Pin_23
  N4: Zigbee_Thermostat_Bridge.Pin_23, Daikin_Controller.Pin_22

custom parts:
  ESP32-C6-DevKitC-1: ESP32-C6-DevKitC-1 is an entry-level development board based on ESP32-C6-WROOM-1(U), a general-purpose module with a 8 MB SPI flash. This board integrates complete Wi-Fi, Bluetooth LE, Zigbee, and Thread functions.
